// Logisim project Processor.circ as structural Verilog: 4 circuits, main circuit main
module main (
);

  wire clock_1_out, undriven, undriven_4;
  wire [3:0] undriven_3, undriven_5, undriven_6;
  wire [7:0] register_file_1_out_8, register_file_1_out_9, undriven_2, val_A_q, val_B_q;

  ALU ALU ();  // open: out_4, in_2, in_3, in_1
  Register val_A (.D(register_file_1_out_8), .en(undriven), .Q(val_A_q), .clk(clock_1_out));  // open: clr
  Register_File register_file_1 (
    .in_5(undriven_2), .in_6(undriven_4), .in_7(undriven_5), .out_8(register_file_1_out_8), .in_1(undriven),
    .in_2(undriven_3), .out_9(register_file_1_out_9), .in_3(undriven), .in_4(undriven_6));
  Register val_B (.D(register_file_1_out_9), .en(undriven), .Q(val_B_q), .clk(clock_1_out));  // open: clr
  Clock clock_1 (.out(clock_1_out));
endmodule

module ALU (
  input  in_1,
  input  [31:0] in_2,
  input  [31:0] in_3,
  output [31:0] out_4
);

  wire [31:0] adder_1_out, multiplier_1_out;

  Multiplexer #(.width(32), .disabled(0), .enable("false")) multiplexer_1 (
    .in0(adder_1_out), .in1(multiplier_1_out), .out(out_4), .sel(in_1));
  Adder #(.width(32)) adder_1 (.a(in_2), .b(in_3), .out(adder_1_out));  // open: cin, cout
  Multiplier #(.width(32)) multiplier_1 (.a(in_2), .b(in_3), .out(multiplier_1_out));  // open: cin, cout
endmodule

module Register_File (
  input  in_1,
  input  [3:0] in_2,
  input  in_3,
  input  [3:0] in_4,
  input  [7:0] in_5,
  input  in_6,
  input  [3:0] in_7,
  output [7:0] out_8,
  output [7:0] out_9
);

  wire clock_1_out;
  wire [7:0] A_q, B_q, C_q, D_q, demultiplexer_2_out0, demultiplexer_2_out1, demultiplexer_2_out2,
       demultiplexer_2_out3, demultiplexer_2_out4, demultiplexer_2_out5, demultiplexer_2_out6,
       demultiplexer_2_out7, demultiplexer_2_out8, demultiplexer_2_out9, demultiplexer_2_out10,
       demultiplexer_2_out11, demultiplexer_2_out12, demultiplexer_2_out13, demultiplexer_2_out14,
       demultiplexer_2_out15, E_q, F_q, G_q, H_q, I_q, J_q, K_q, L_q, M_q, N_q, rbp_q, rsp_q;
  wire [15:0] demultiplexer_1_out0;

  Demultiplexer #(.select(4), .enable("false")) demultiplexer_1 (
    .out0(demultiplexer_1_out0[0]), .out1(demultiplexer_1_out0[1]), .out2(demultiplexer_1_out0[2]),
    .out3(demultiplexer_1_out0[3]), .out4(demultiplexer_1_out0[4]), .out5(demultiplexer_1_out0[5]),
    .out6(demultiplexer_1_out0[6]), .out7(demultiplexer_1_out0[7]), .out8(demultiplexer_1_out0[8]),
    .out9(demultiplexer_1_out0[9]), .out10(demultiplexer_1_out0[10]), .out11(demultiplexer_1_out0[11]),
    .out12(demultiplexer_1_out0[12]), .out13(demultiplexer_1_out0[13]), .out14(demultiplexer_1_out0[14]),
    .out15(demultiplexer_1_out0[15]), .in(in_6), .sel(in_7));
  Demultiplexer #(.select(4), .width(8), .disabled(0)) demultiplexer_2 (
    .out0(demultiplexer_2_out0), .out1(demultiplexer_2_out1), .out2(demultiplexer_2_out2),
    .out3(demultiplexer_2_out3), .out4(demultiplexer_2_out4), .out5(demultiplexer_2_out5),
    .out6(demultiplexer_2_out6), .out7(demultiplexer_2_out7), .out8(demultiplexer_2_out8),
    .out9(demultiplexer_2_out9), .out10(demultiplexer_2_out10), .out11(demultiplexer_2_out11),
    .out12(demultiplexer_2_out12), .out13(demultiplexer_2_out13), .out14(demultiplexer_2_out14),
    .out15(demultiplexer_2_out15), .in(in_5), .sel(in_7), .en(in_6));
  Clock clock_1 (.out(clock_1_out));
  Register A (.D(demultiplexer_2_out0), .en(demultiplexer_1_out0[0]), .Q(A_q), .clk(clock_1_out));  // open: clr
  Register B (.D(demultiplexer_2_out1), .en(demultiplexer_1_out0[1]), .Q(B_q), .clk(clock_1_out));  // open: clr
  Register C (.D(demultiplexer_2_out2), .en(demultiplexer_1_out0[2]), .Q(C_q), .clk(clock_1_out));  // open: clr
  Register D (.D(demultiplexer_2_out3), .en(demultiplexer_1_out0[3]), .Q(D_q), .clk(clock_1_out));  // open: clr
  Register E (.D(demultiplexer_2_out4), .en(demultiplexer_1_out0[4]), .Q(E_q), .clk(clock_1_out));  // open: clr
  Register F (.D(demultiplexer_2_out5), .en(demultiplexer_1_out0[5]), .Q(F_q), .clk(clock_1_out));  // open: clr
  Register G (.D(demultiplexer_2_out6), .en(demultiplexer_1_out0[6]), .Q(G_q), .clk(clock_1_out));  // open: clr
  Register H (.D(demultiplexer_2_out7), .en(demultiplexer_1_out0[7]), .Q(H_q), .clk(clock_1_out));  // open: clr
  Register I (.D(demultiplexer_2_out8), .en(demultiplexer_1_out0[8]), .Q(I_q), .clk(clock_1_out));  // open: clr
  Register J (.D(demultiplexer_2_out9), .en(demultiplexer_1_out0[9]), .Q(J_q), .clk(clock_1_out));  // open: clr
  Register K (.D(demultiplexer_2_out10), .en(demultiplexer_1_out0[10]), .Q(K_q), .clk(clock_1_out));  // open: clr
  Register L (.D(demultiplexer_2_out11), .en(demultiplexer_1_out0[11]), .Q(L_q), .clk(clock_1_out));  // open: clr
  Register M (.D(demultiplexer_2_out12), .en(demultiplexer_1_out0[12]), .Q(M_q), .clk(clock_1_out));  // open: clr
  Register N (.D(demultiplexer_2_out13), .en(demultiplexer_1_out0[13]), .Q(N_q), .clk(clock_1_out));  // open: clr
  Register rbp (.D(demultiplexer_2_out14), .en(demultiplexer_1_out0[14]), .Q(rbp_q), .clk(clock_1_out));  // open: clr
  Register rsp (.D(demultiplexer_2_out15), .en(demultiplexer_1_out0[15]), .Q(rsp_q), .clk(clock_1_out));  // open: clr
  Multiplexer #(.select(4), .width(8), .disabled(0)) multiplexer_1 (
    .in0(A_q), .in1(B_q), .in2(C_q), .in3(D_q), .in4(E_q), .in5(F_q), .in6(G_q), .in7(H_q), .in8(I_q),
    .in9(J_q), .in10(K_q), .in11(L_q), .in12(M_q), .in13(N_q), .in14(rbp_q), .in15(rsp_q), .out(out_8),
    .sel(in_2), .en(in_1));
  Multiplexer #(.select(4), .width(8), .disabled(0)) multiplexer_2 (
    .in0(A_q), .in1(B_q), .in2(C_q), .in3(D_q), .in4(E_q), .in5(F_q), .in6(G_q), .in7(H_q), .in8(I_q),
    .in9(J_q), .in10(K_q), .in11(L_q), .in12(M_q), .in13(N_q), .in14(rbp_q), .in15(rsp_q), .out(out_9),
    .sel(in_4), .en(in_3));
endmodule

module Memory (
  input  [7:0] Address_Bus,
  input  [7:0] in_2,
  input  in_3,
  input  _10___Write,
  input  in_5,
  output [7:0] Data_Bus
);

  wire _01_out, _10_out, clock_1_out, sel_out;
  wire [7:0] ram_1_data, register_1_q;

  Register register_1 (.D(Address_Bus), .Q(register_1_q), .clk(clock_1_out));  // open: en, clr
  and _01 (_01_out, ~_10___Write, in_5);  // AND_Gate
  and _10 (_10_out, _10___Write, ~in_5);  // AND_Gate
  xor sel (sel_out, _10___Write, in_5);
  Clock clock_1 (.out(clock_1_out));
  RAM #(.bus("separate")) ram_1 (
    .addr(register_1_q), .din(in_2), .data(ram_1_data), .str(_01_out), .sel(sel_out), .clk(clock_1_out),
    .ld(_10_out));  // open: clr
  ROM rom_1 (.addr(register_1_q), .data(ram_1_data), .sel(in_3));
  Register register_2 (.D(ram_1_data), .Q(Data_Bus), .clk(clock_1_out));  // open: en, clr

  // Notes on the sheet:
  //   00 - Do Nothing
  //   01 - Read
  //   Data_in
  //   RAM
  //   store_data_en
  //   load_data_en
  //   ROM
  //   contents of rom_1 (hex, n*v repeats v):
  //   f 0 0 0 f
  //   ROM_select_en
endmodule
